# Fritzing sketch tamrin1 (3) (saved by Fritzing 0.9.4)
breadboards: 1

parts:
  Part1 = Arduino Uno (Rev3) - ICSP
  LED2 = LED - 3mm [color="Red (633nm)" package="3 mm [THT]"]
  LED3 = LED - 3mm [color="Yellow (595nm)" package="3 mm [THT]"]
  LED4 = LED - 3mm [color="Blue (525nm)" package="3 mm [THT]"]
  S1 = Pushbutton [package="[SMD]"]
  LED5 = LED - 3mm [color="Red (633nm)" package="3 mm [THT]"]
  LED6 = LED - 3mm [color="Blue (525nm)" package="3 mm [THT]"]
  LED7 = LED - 3mm [color="Yellow (595nm)" package="3 mm [THT]"]

nets:
  N1: Part1.RESET, S1.Pin_1, S1.Pin_2
  N2: Part1.GND, LED2.cathode, LED3.cathode, LED4.cathode, S1.Pin_3, S1.Pin_4, LED5.cathode, LED6.cathode, LED7.cathode
